# Fritzing sketch Stackin Robojam (saved by Fritzing 0.9.3b)
stripboards: 1

parts:
  MH-ET_LIVE_ESP32_DEVKIT1 = MH-ET LIVE ESP32 DEVKIT 38 pins
  L298N1 = L298N DC motor driver
  M1 = DC Motor
  M2 = DC Motor
  VCC2 = Battery
  S1 = Toggle Switch spst [package=THT]
  J1 = Basic Servo
  J2 = Basic Servo

nets:
  5V: MH-ET_LIVE_ESP32_DEVKIT1.5V, L298N1.5V, J1.vcc, J2.vcc
  GND: MH-ET_LIVE_ESP32_DEVKIT1.GND, L298N1.GND, VCC2.-, J1.gnd, J2.gnd
  N1: MH-ET_LIVE_ESP32_DEVKIT1.IO23, J1.pulse
  N2: MH-ET_LIVE_ESP32_DEVKIT1.IO22, J2.pulse
  N3: MH-ET_LIVE_ESP32_DEVKIT1.IO19, L298N1.ENA
  N4: MH-ET_LIVE_ESP32_DEVKIT1.IO18, L298N1.IN1
  N5: MH-ET_LIVE_ESP32_DEVKIT1.IO5, L298N1.IN2
  N6: MH-ET_LIVE_ESP32_DEVKIT1.IO17, L298N1.IN3
  N7: MH-ET_LIVE_ESP32_DEVKIT1.IO16, L298N1.IN4
  N8: MH-ET_LIVE_ESP32_DEVKIT1.IO15, L298N1.ENB
  N9: L298N1.OUT1, M1.pin_2
  N10: L298N1.OUT2, M1.pin_1
  N11: L298N1.OUT3, M2.pin_2
  N12: L298N1.OUT4, M2.pin_1
  N13: L298N1.12V, S1.L1
  N14: VCC2.+, S1.COM

custom parts:
  MH-ET LIVE ESP32 DEVKIT 38 pins: http://mh.nodebb.com/topic/2/mh-et-live-esp32-devkit
  L298N DC motor driver: 2x DC motor driver with 78M05 positive voltage regulator (7..35 V) L298N: max 46 V, 2 A Set 5 V Enable jumper to enable 5 V regultor (needed for the L298N) and +5 V output at screw terminal or supply external +5 V at screw terminal Set ENA and/or ENB to +5 V to enable motor permanently or supply ENA and/or ENB with PWM signal IN1 and IN2 set rotation directory for motor A (OUT1/OUT2) IN2 and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
  Battery: Your standard 2x 18650 battery pack (7,4 Volts)
  Toggle Switch spst: Toggle Switch single pole single throw
