# Fritzing sketch cultivo hidroponico (saved by Fritzing 0.9.3b)

parts:
  VCC1 = Battery
  M3 = DC Motor
  M4 = 1 chan 5v relay module
  IC1 = DS3231MZ Real Time Clock
  M5 = DC Motor
  E1 = ESP32-Cam
  IC2 = Voltage Regulator [package=to-220-alt]

nets:
  N1: VCC1.-, M3.pin_2, IC1.Pin_5, M5.pin_2, E1.GND#15, IC2.GND
  N2: VCC1.+, M3.pin_1, M4.pin_5, IC2.IN
  N3: M4.pin_1, E1.3.3V
  N4: M4.pin_2, E1.GND#1
  N5: M4.pin_3, E1.GPIO_12
  N6: M4.pin_4, M5.pin_1
  N7: IC1.Pin_2, E1.5V, IC2.OUT
  N8: IC1.Pin_7, E1.GPIO_13
  N9: IC1.Pin_8, E1.GPIO_15

notes:
  y esta pensado para automatizarse los15 dias
  los motores son motobombas

custom parts:
  1 chan 5v relay module: 1 Channel 5V Relay Module Board Shield with Optocoupler Support High and Low Level Trigger for Arduino.
  DS3231MZ Real Time Clock: DS3231MZ Real Time Clock. SO-8 surface mount version.
