# Fritzing sketch robot.cultivador (saved by Fritzing 1.0.1rc)
stripboards: 1

parts:
  A2 = Arducam mini 2mp plus
  S1 = H-Bridge with L298N
  U1 = LM2596 step down module
  U2 = LM2596 step down module
  M1 = DFR sen0308 [package=THT]
  BAT1 = Lithium Ion Polymer Battery 11.1v 5000mah
  A3 = SIM 4G A7680C module
  M2 = DOIT Esp32 DevKit v1 (30 pins long, 11 pins width) [part_number=ESP32S-PIN30]
  U3 = SWITCH-SPST-2 [package=switch-spst-vertical]
  Componente1 = Jtron 1 Channel Optoisolated Relay Module [package=relay]
  Mini_Water_Pump_3-6VDC1 = Mini Water Pump 3-6VDC [part_number="Mini Water Pump 3-6VDC" chip_label=IC package="DIP (Dual Inline) [THT]"]
  DHT1 = DHT22 Humidity and Temperature Sensor
  J1 = Basic Servo
  M3 = DC Motor [voltage_(max)=6V voltage_(min)=3V]
  M4 = DC Motor [voltage_(max)=6V voltage_(min)=3V]
  M5 = DC Motor [voltage_(max)=6V voltage_(min)=3V]
  M6 = DC Motor [voltage_(max)=6V voltage_(min)=3V]

nets:
  N1: A2.Pin_1, M2.D22
  N2: A2.Pin_2, M2.D21
  5V: A2.Pin_3, S1.5V, U1.OUT+, M1.pin4, M2.VIN, DHT1.VDD, J1.vcc
  GND: A2.Pin_4, S1.GND, U1.IN-, U1.OUT-, U2.IN-, U2.OUT-, M1.pin2, M1.pin3, BAT1.negative, A3.Pin_6, M2.GND, M2.D34, Componente1.GND, DHT1.GND, J1.gnd
  N3: A2.Pin_5, M2.D18
  N4: A2.Pin_6, M2.D19
  N5: A2.Pin_7, M2.D23
  N6: A2.Pin_8, S1.IN1, M2.D15, M2.D5, M2.D12
  N7: S1.12V, U1.IN+, U2.IN+, U3.P
  N8: S1.IN2, M2.D14
  N9: S1.IN3, M2.D32
  N10: S1.IN4, M2.D33
  N11: S1.M1-01, M3.pin_2, M4.pin_2
  N12: S1.M1-02, M3.pin_1, M4.pin_1
  N13: S1.M2-01, M5.pin_1, M6.pin_1
  N14: S1.M2-02, M5.pin_2, M6.pin_2
  N15: U2.OUT+, A3.Pin_2
  N16: BAT1.positive, U3.O
  N17: A3.Pin_4, M2.TX2
  N18: A3.Pin_5, M2.RX2
  N19: M2.D4, DHT1.DATA
  N20: M2.D25, Componente1.IN1
  N21: M2.D13, J1.pulse
  N22: Componente1.NC, Mini_Water_Pump_3-6VDC1.+M
  N23: Componente1.MAIN, Mini_Water_Pump_3-6VDC1.-M

notes:
  se pone a 4 voltios
  se pone a 5 voltios

custom parts:
  Arducam mini 2mp plus: ArduCAM-2MP-Plus is a high-definition 2MP SPI camera, which reduces the complexity of the camera control interface.
  H-Bridge with L298N: h-bridge
  LM2596 step down module: LM2596 DC-DC step down power supply module 3 A.
  DFR sen0308: This is a new type of waterproof soil moisture sensor introduced by DFRobot. Compared with the previous version of the soil moisture sensor, it has increased waterproof performance, optimized corrosion resistance, increased plate length and optimized circuit performance. Compared with the resistive sensor, the capacitive soil moisture sensor solves the problem that the resistive sensor is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
  SIM 4G A7680C module: The 4G SIM module A7680C has the ability to send SMS messages, listen, call, GPRS, ... like a phone but has the smallest size among SIM modules (27mm x 26mm).
  DOIT Esp32 DevKit v1 (30 pins long, 11 pins width): The DOIT Esp32 DevKit v1 is one of the development board created by DOIT to evaluate the ESP-WROOM-32 module. It is based on the ESP32 microcontroller that boasts Wifi, Bluetooth, Ethernet and Low Power support all in a single chip. (vanepp) made breadboard work, adjusted pin numbering and labels and reduced size of schematic and cleaned up pcb. This chip is 30pins long (2 x15) and 11 pins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
